# Fritzing sketch Morsecode_with_active_Buzzer (saved by Fritzing 0.9.3b)
breadboards: 1

parts:
  Bauteil1 = Arduino Uno (Rev3)
  R1 = Trimmer Potentiometer [maximum_resistance=10kΩ package=THT]
  J1 = Piezo Speaker

nets:
  N1: Bauteil1.A0, R1.wiper
  N2: Bauteil1.D12/MISO, J1.pin2
  N3: Bauteil1.GND, R1.leg2, J1.pin1
  N4: Bauteil1.5V, R1.leg1
